// Digital circuit 6bitALU.dig as structural Verilog
module _6bitALU (
  input  [5:0] A_5_0,
  input  [5:0] B_5_0,
  input  [1:0] OP_1_0,
  output ZF,
  output SF,
  output [5:0] O_5_0
);

  wire or_1_out;
  wire [5:0] _6bit_not_1_y_5_0, _6bit_rightshifter_1_o_5_0, add_sub_1_o_5_0;

  _6bit_NOT _6bit_not_1 (.A_5_0(A_5_0), .Y_5_0(_6bit_not_1_y_5_0));
  ADD_SUB add_sub_1 (.A_5_0(A_5_0), .B_5_0(B_5_0), .Sel(OP_1_0[0]), .O_5_0(add_sub_1_o_5_0));  // open: CF
  _6bit_RightShifter _6bit_rightshifter_1 (.A_5_0(A_5_0), .B_5_0(B_5_0), .O_5_0(_6bit_rightshifter_1_o_5_0));
  Multiplexer #(.Selector_Bits(2), .Bits(6)) multiplexer_1 (
    .sel(OP_1_0), .in_0(_6bit_not_1_y_5_0), .in_1(add_sub_1_o_5_0), .in_2(add_sub_1_o_5_0),
    .in_3(_6bit_rightshifter_1_o_5_0), .out(O_5_0));
  or or_1 (or_1_out, O_5_0[0], O_5_0[1], O_5_0[2], O_5_0[3], O_5_0[4], O_5_0[5]);
  not not_1 (ZF, or_1_out);

  assign SF = O_5_0[5];

  // Other names for the same wires on the sheet: A[5:0] = A_5_0; B[5:0] = B_5_0; OP_0 = OP_1_0[0]; OP_1 = OP_1_0[1];
  //   R[5:0] = O_5_0
endmodule
