// Digital circuit 6bit CPU new.dig as structural Verilog
module _6bit_CPU_new (
  input  [17:0] Wrd_17_0,
  input  CLK,
  input  WE,
  input  PC_EN,
  input  [2:0] Wr_2_0,
  output [17:0] RD2_17_0,
  output [5:0] result,
  output [1:0] reg1,
  output [1:0] reg2,
  output [5:0] reg1_value,
  output [1:0] op,
  output [5:0] value_part
);

  wire CPU_CLK, Imm_sel, JMP_SEL, REG_EN, SF, ZF;
  wire [2:0] _3bit_pc_adder_1_o_2_0, _3bit_program_counter_1_dout_2_0, multiplexer_1_out;
  wire [3:0] Opcode, value;
  wire [5:0] _6bitreg_set_1_b_5_0, XX;

  Multiplexer #(.Bits(3)) multiplexer_1 (
    .sel(JMP_SEL), .in_0(_3bit_pc_adder_1_o_2_0), .in_1({reg1, reg2[1]}), .out(multiplexer_1_out));
  _3bit_program_counter _3bit_program_counter_1 (
    .Din_2_0(multiplexer_1_out), .CLK(CPU_CLK), .Dout_2_0(_3bit_program_counter_1_dout_2_0));
  and and_1 (CPU_CLK, PC_EN, CLK);
  _3bit_PC_adder _3bit_pc_adder_1 (.I_2_0(_3bit_program_counter_1_dout_2_0), .O_2_0(_3bit_pc_adder_1_o_2_0));
  _8x18_SRAM _8x18_sram_1 (
    .RA1_2_0(_3bit_program_counter_1_dout_2_0), .RA2_2_0(3'b000), .WA_2_0(Wr_2_0), .Wrd_17_0(Wrd_17_0),
    .WE(WE), .CLK(CLK), .RD1_17_0({Opcode, reg1, reg2, value, XX}), .RD2_17_0(RD2_17_0));
  _6bitREG_set _6bitreg_set_1 (
    .Wrd_5_0(result), .Wr_1_0(reg1), .WE(REG_EN), .CLK(CPU_CLK), .RA_1_0(reg1), .RB_1_0(reg2),
    .A_5_0(reg1_value), .B_5_0(_6bitreg_set_1_b_5_0));
  _4bit_CU _4bit_cu_1 (
    .Opcode_3_0(Opcode), .ZF(ZF), .SF(SF), .Op_1_0(op), .REG_EN(REG_EN), .Imm_sel(Imm_sel), .Jmp_sel(JMP_SEL));
  _6bitALU _6bitalu_1 (.A_5_0(reg1_value), .B_5_0(value_part), .OP_1_0(op), .ZF(ZF), .SF(SF), .O_5_0(result));
  Multiplexer #(.Bits(6)) multiplexer_2 (
    .sel(Imm_sel), .in_0(_6bitreg_set_1_b_5_0), .in_1({reg2, value}), .out(value_part));

  // Other names for the same wires on the sheet: value[5:4] = reg2; JMP_ADDRESS[2:0] = {reg1, reg2[1]};
  //   A[5:0] = reg1_value; B[5:0] = value_part; RD2[17:0] = RD2_17_0; Wr[2:0] = Wr_2_0; Wrd[17:0] = Wrd_17_0
endmodule
