// Digital circuit 6bitREG set.dig as structural Verilog
module _6bitREG_set (
  input  [5:0] Wrd_5_0,
  input  [1:0] Wr_1_0,
  input  WE,
  input  [1:0] RA_1_0,
  input  [1:0] RB_1_0,
  input  CLK,
  output [5:0] A_5_0,
  output [5:0] B_5_0
);

  wire A0, A1, A2, D0, D1, D2, decoder_1_out_3;
  wire [5:0] R0, R1, R2;

  and and_1 (D0, A0, WE);
  and and_2 (D2, A2, WE);
  Decoder #(.Selector_Bits(2)) decoder_1 (.sel(Wr_1_0), .out_0(A0), .out_1(A1), .out_2(A2), .out_3(decoder_1_out_3));
  and and_3 (D1, A1, WE);
  _6bit_reg _6bit_reg_1 (.Din_5_0(Wrd_5_0), .Sel(D2), .CLK(CLK), .Dout_5_0(R2));
  _6bit_reg _6bit_reg_2 (.Din_5_0(Wrd_5_0), .Sel(D1), .CLK(CLK), .Dout_5_0(R1));
  _6bit_reg _6bit_reg_3 (.Din_5_0(Wrd_5_0), .Sel(D0), .CLK(CLK), .Dout_5_0(R0));
  Multiplexer #(.Bits(6), .Selector_Bits(2)) multiplexer_1 (
    .sel(RA_1_0), .in_0(R0), .in_1(R1), .in_2(R2), .in_3({6{1'b0}}), .out(A_5_0));
  Multiplexer #(.Selector_Bits(2), .Bits(6)) multiplexer_2 (
    .sel(RB_1_0), .in_0(R0), .in_1(R1), .in_2(R2), .in_3({6{1'b0}}), .out(B_5_0));
  // also tied to GND on the sheet: decoder_1_out_3
endmodule
