// Digital circuit 6bit_NOT.dig as structural Verilog
module _6bit_NOT (
  input  [5:0] A_5_0,
  output [5:0] Y_5_0
);

  not not_1 (Y_5_0[5], A_5_0[5]);
  not not_2 (Y_5_0[4], A_5_0[4]);
  not not_3 (Y_5_0[3], A_5_0[3]);
  not not_4 (Y_5_0[2], A_5_0[2]);
  not not_5 (Y_5_0[1], A_5_0[1]);
  not not_6 (Y_5_0[0], A_5_0[0]);
endmodule
