// Digital circuit 5bit CU.dig as structural Verilog
module _5bit_CU (
  input  [3:0] Opcode_3_0,
  input  CF,
  output [1:0] Op_1_0,
  output Imm_sel,
  output REG_EN,
  output JMP_sel
);

  wire and_1_out, and_3_out, and_4_out, and_5_out, or_1_out;

  and and_1 (and_1_out, ~Opcode_3_0[2], ~Opcode_3_0[3]);  // And
  and and_2 (Imm_sel, Opcode_3_0[2], ~Opcode_3_0[3]);  // And
  and and_3 (and_3_out, ~Opcode_3_0[2], Opcode_3_0[3]);  // And
  and and_4 (and_4_out, ~Opcode_3_0[0], ~Opcode_3_0[1]);  // And
  and and_5 (and_5_out, Opcode_3_0[0], ~Opcode_3_0[1], ~CF);  // And
  or or_1 (or_1_out, and_4_out, and_5_out);
  or or_2 (REG_EN, and_1_out, Imm_sel);
  and and_6 (JMP_sel, and_3_out, or_1_out);

  assign Op_1_0 = Opcode_3_0[1:0];

  // Other names for the same wires on the sheet: jmp_type[1:0] = Opcode_3_0[1:0]
endmodule
