// Digital circuit 5bit ADD.dig as structural Verilog
module _5bit_ADD (
  input  [4:0] A_4_0,
  input  [4:0] B_4_0,
  output [4:0] O_4_0,
  output CF
);

  wire fa_2_cout, fa_3_cout, fa_4_cout, fa_5_cout;

  FA fa_1 (.X(A_4_0[4]), .Y(B_4_0[4]), .Cin(fa_2_cout), .S(O_4_0[4]), .Cout(CF));
  FA fa_2 (.X(A_4_0[3]), .Y(B_4_0[3]), .Cin(fa_3_cout), .S(O_4_0[3]), .Cout(fa_2_cout));
  FA fa_3 (.X(A_4_0[2]), .Y(B_4_0[2]), .Cin(fa_4_cout), .S(O_4_0[2]), .Cout(fa_3_cout));
  FA fa_4 (.X(A_4_0[1]), .Y(B_4_0[1]), .Cin(fa_5_cout), .S(O_4_0[1]), .Cout(fa_4_cout));
  FA fa_5 (.X(A_4_0[0]), .Y(B_4_0[0]), .Cin(1'b0), .S(O_4_0[0]), .Cout(fa_5_cout));

  // Other names for the same wires on the sheet: A_0 = A_4_0[0]; A_1 = A_4_0[1]; A_2 = A_4_0[2]; A_3 = A_4_0[3];
  //   A_4 = A_4_0[4]; B_0 = B_4_0[0]; B_1 = B_4_0[1]; B_2 = B_4_0[2]; B_3 = B_4_0[3]; B_4 = B_4_0[4]; O_0 = O_4_0[0];
  //   O_1 = O_4_0[1]; O_2 = O_4_0[2]; O_3 = O_4_0[3]; O_4 = O_4_0[4]
endmodule
