// Digital circuit 5bit CPU.dig as structural Verilog
module _5bit_CPU (
  input  [17:0] Wrd_17_0,
  input  CLK,
  input  WE,
  input  PC_EN,
  input  [3:0] Wr_3_0,
  output [17:0] RD2_17_0,
  output [4:0] R,
  output [1:0] reg1,
  output [1:0] reg2,
  output [4:0] reg1_value,
  output [1:0] op,
  output [4:0] value_part,
  output [3:0] address_jmp
);

  wire CF, CPU_CLK, Imm_sel, jmp_sel, REG_EN;
  wire [2:0] value;
  wire [3:0] _4bit_pc_adder_1_o_3_0, _4bit_program_counter_1_dout_3_0, multiplexer_1_out, Opcode;
  wire [4:0] _5bit_reg_set_1_b_4_0;
  wire [6:0] XX;

  Multiplexer #(.Bits(4)) multiplexer_1 (
    .sel(jmp_sel), .in_0(_4bit_pc_adder_1_o_3_0), .in_1(address_jmp), .out(multiplexer_1_out));
  _4bit_PC_adder _4bit_pc_adder_1 (.I_3_0(_4bit_program_counter_1_dout_3_0), .O_3_0(_4bit_pc_adder_1_o_3_0));
  _4bit_program_counter _4bit_program_counter_1 (
    .Din_3_0(multiplexer_1_out), .CLK(CPU_CLK), .Dout_3_0(_4bit_program_counter_1_dout_3_0));
  and and_1 (CPU_CLK, PC_EN, CLK);
  _9x18_SRAM _9x18_sram_1 (
    .RA1_3_0(_4bit_program_counter_1_dout_3_0), .RA2_3_0(4'b0000), .WA_3_0(Wr_3_0), .Wrd_17_0(Wrd_17_0),
    .WE(WE), .CLK(CLK), .RD1_17_0({Opcode, address_jmp, value, XX}), .RD2_17_0(RD2_17_0));
  _5bit_reg_set _5bit_reg_set_1 (
    .Wrd_4_0(R), .Wr_1_0(address_jmp[3:2]), .WE(REG_EN), .CLK(CPU_CLK), .RA_1_0(address_jmp[3:2]),
    .RB_1_0(address_jmp[1:0]), .A_4_0(reg1_value), .B_4_0(_5bit_reg_set_1_b_4_0));
  _5bit_ALU _5bit_alu_1 (.A_4_0(reg1_value), .B_4_0(value_part), .OP_1_0(op), .O_4_0(R), .CF(CF));
  _5bit_CU _5bit_cu_1 (
    .Opcode_3_0(Opcode), .CF(CF), .Op_1_0(op), .REG_EN(REG_EN), .Imm_sel(Imm_sel), .JMP_sel(jmp_sel));
  Multiplexer #(.Bits(5)) multiplexer_2 (
    .sel(Imm_sel), .in_0(_5bit_reg_set_1_b_4_0), .in_1({address_jmp[1:0], value}), .out(value_part));

  assign reg1 = address_jmp[3:2];
  assign reg2 = address_jmp[1:0];

  // Other names for the same wires on the sheet: jmp_address[3:0] = address_jmp; value[4:3] = address_jmp[1:0];
  //   A[4:0] = reg1_value; B[4:0] = value_part; RD2[17:0] = RD2_17_0; Wr[3:0] = Wr_3_0; Wrd[17:0] = Wrd_17_0
endmodule
