// Digital circuit 3bit program counter.dig as structural Verilog
module _3bit_program_counter (
  input  CLK,
  input  [2:0] Din_2_0,
  output [2:0] Dout_2_0
);

  // _1bit_reg _1bit_reg_1: pin names not known; wires that end beside it: Din_2_0[0], 1'b1, CLK, Dout_2_0[0]
  // _1bit_reg _1bit_reg_2: pin names not known; wires that end beside it: Din_2_0[1], 1'b1, CLK, Dout_2_0[1]
  // _1bit_reg _1bit_reg_3: pin names not known; wires that end beside it: Din_2_0[2], 1'b1, CLK, Dout_2_0[2]

  // Other names for the same wires on the sheet: D_0 = Din_2_0[0]; D_1 = Din_2_0[1]; D_2 = Din_2_0[2];
  //   O_0 = Dout_2_0[0]; O_1 = Dout_2_0[1]; O_2 = Dout_2_0[2]
endmodule
