// Digital circuit 5bit ADD.dig as structural Verilog
module _5bit_ADD (
  input  [4:0] A_4_0,
  input  [4:0] B_4_0,
  output [4:0] O_4_0
);

  wire _1bit_fa_1_p5, _1bit_fa_2_p4, _1bit_fa_3_p4, _1bit_fa_4_p4, CF;

  // _1bit_FA _1bit_fa_1: pin names not known; wires that end beside it: CF, B_4_0[4], O_4_0[4], A_4_0[4], _1bit_fa_1_p5, _1bit_fa_1_p5
  // _1bit_FA _1bit_fa_2: pin names not known; wires that end beside it: B_4_0[3], O_4_0[3], A_4_0[3], _1bit_fa_2_p4, _1bit_fa_2_p4
  // _1bit_FA _1bit_fa_3: pin names not known; wires that end beside it: B_4_0[2], O_4_0[2], A_4_0[2], _1bit_fa_3_p4, _1bit_fa_3_p4
  // _1bit_FA _1bit_fa_4: pin names not known; wires that end beside it: B_4_0[1], O_4_0[1], A_4_0[1], _1bit_fa_4_p4, _1bit_fa_4_p4
  // _1bit_FA _1bit_fa_5: pin names not known; wires that end beside it: B_4_0[0], O_4_0[0], A_4_0[0], 1'b0

  // Other names for the same wires on the sheet: A_0 = A_4_0[0]; A_1 = A_4_0[1]; A_2 = A_4_0[2]; A_3 = A_4_0[3];
  //   A_4 = A_4_0[4]; B_0 = B_4_0[0]; B_1 = B_4_0[1]; B_2 = B_4_0[2]; B_3 = B_4_0[3]; B_4 = B_4_0[4]; O_0 = O_4_0[0];
  //   O_1 = O_4_0[1]; O_2 = O_4_0[2]; O_3 = O_4_0[3]; O_4 = O_4_0[4]
endmodule
