// Digital circuit 5bit ALU_.dig as structural Verilog
module _5bit_ALU (
  input  [4:0] A_4_0,
  input  [4:0] B_4_0,
  input  [1:0] OP_1_0,
  output [4:0] O_4_0,
  output ZF,
  output SF
);

  wire [4:0] _5bit_add_1_o_4_0, _5bit_not_1_o_4_0, _5bit_rol_1_o_4_0;

  _5bit_ADD _5bit_add_1 (.A_4_0(A_4_0), .B_4_0(B_4_0), .O_4_0(_5bit_add_1_o_4_0));
  _5bit_NOT _5bit_not_1 (.A_4_0(A_4_0), .O_4_0(_5bit_not_1_o_4_0));
  _5bit_ROL _5bit_rol_1 (.A_4_0(A_4_0), .B_4_0(B_4_0), .O_4_0(_5bit_rol_1_o_4_0));
  Multiplexer #(.Selector_Bits(2), .Bits(5)) multiplexer_1 (
    .sel(OP_1_0), .in_0(_5bit_not_1_o_4_0), .in_1(_5bit_add_1_o_4_0), .in_2(_5bit_rol_1_o_4_0),
    .in_3({5{1'b0}}), .out(O_4_0));
  nor nor_1 (ZF, O_4_0[0], O_4_0[1], O_4_0[2], O_4_0[3], O_4_0[4]);

  assign SF = O_4_0[4];

  // Other names for the same wires on the sheet: A[4:0] = A_4_0; B[4:0] = B_4_0; O[4:0] = O_4_0; OP_0 = OP_1_0[0];
  //   OP_1 = OP_1_0[1]
endmodule
