// Digital circuit 5bit CPU.dig as structural Verilog
module _5bit_CPU (
  input  [14:0] Wrd_14_0,
  input  CLK,
  input  WE,
  input  PC_EN,
  input  [2:0] Wr_2_0,
  output [14:0] RD2_14_0,
  output [4:0] R,
  output [2:0] reg1,
  output [2:0] reg2,
  output [4:0] reg1_number,
  output [1:0] op,
  output [4:0] Imm_number
);

  wire CPU_CLK, Imm_sel, jmp_sel, REG_EN, SF, ZF;
  wire [1:0] \int ;
  wire [2:0] _3bit_pc_adder_1_o_2_0, _3bit_program_counter_1_dout_2_0, multiplexer_1_out, XX;
  wire [3:0] Opcode;
  wire [4:0] _5bit_reg_set_with_6_reg_1_b_4_0;

  Multiplexer #(.Bits(3)) multiplexer_1 (
    .sel(jmp_sel), .in_0(_3bit_pc_adder_1_o_2_0), .in_1(reg1), .out(multiplexer_1_out));
  _3bit_PC_adder _3bit_pc_adder_1 (.I_2_0(_3bit_program_counter_1_dout_2_0), .O_2_0(_3bit_pc_adder_1_o_2_0));
  _3bit_program_counter _3bit_program_counter_1 (
    .Din_2_0(multiplexer_1_out), .CLK(CPU_CLK), .Dout_2_0(_3bit_program_counter_1_dout_2_0));
  and and_1 (CPU_CLK, PC_EN, CLK);
  _8x15_SRAM _8x15_sram_1 (
    .RA1_2_0(_3bit_program_counter_1_dout_2_0), .RA2_2_0(3'b000), .WA_2_0(Wr_2_0), .Wrd_14_0(Wrd_14_0),
    .WE(WE), .CLK(CLK), .RD1_14_0({Opcode, reg1, reg2, \int , XX}), .RD2_14_0(RD2_14_0));
  _5bit_CU _5bit_cu_1 (
    .Opcode_3_0(Opcode), .ZF(ZF), .SF(SF), .Op_1_0(op), .REG_EN(REG_EN), .Imm_sel(Imm_sel), .Jmp_sel(jmp_sel));
  _5bit_reg_set_with_6_reg _5bit_reg_set_with_6_reg_1 (
    .Wrd_4_0(R), .Wr_2_0(reg1), .WE(REG_EN), .CLK(CPU_CLK), .RA_2_0(reg1), .RB_2_0(reg2),
    .A_4_0(reg1_number), .B_4_0(_5bit_reg_set_with_6_reg_1_b_4_0));
  _5bit_ALU _5bit_alu_1 (.A_4_0(reg1_number), .B_4_0(Imm_number), .OP_1_0(op), .O_4_0(R), .ZF(ZF), .SF(SF));
  Multiplexer #(.Bits(5)) multiplexer_2 (
    .sel(Imm_sel), .in_0(_5bit_reg_set_with_6_reg_1_b_4_0), .in_1({reg2, \int }), .out(Imm_number));

  // Other names for the same wires on the sheet: int[4:2] = reg2; A[4:0] = reg1_number; B[4:0] = Imm_number;
  //   RD2[14:0] = RD2_14_0; Wr[2:0] = Wr_2_0; Wrd[14:0] = Wrd_14_0
endmodule
