// Digital circuit 5bit NOT.dig as structural Verilog
module _5bit_NOT (
  input  [4:0] A_4_0,
  output [4:0] O_4_0
);

  not not_1 (O_4_0[0], A_4_0[0]);
  not not_2 (O_4_0[1], A_4_0[1]);
  not not_3 (O_4_0[2], A_4_0[2]);
  not not_4 (O_4_0[3], A_4_0[3]);
  not not_5 (O_4_0[4], A_4_0[4]);
endmodule
