// Digital circuit 5bit reg set with 6 reg.dig as structural Verilog
module _5bit_reg_set_with_6_reg (
  input  [4:0] Wrd_4_0,
  input  [2:0] Wr_2_0,
  input  WE,
  input  [2:0] RA_2_0,
  input  [2:0] RB_2_0,
  input  CLK,
  output [4:0] A_4_0,
  output [4:0] B_4_0
);

  wire A0, A1, A2, A3, A4, A5, D0, D1, D2, D3, D4, D5, decoder_1_out_6;
  wire [4:0] R0, R1, R2, R3, R4, R5;

  Decoder #(.Selector_Bits(3)) decoder_1 (
    .sel(Wr_2_0), .out_0(A0), .out_1(A1), .out_2(A2), .out_3(A3), .out_4(A4), .out_5(A5),
    .out_6(decoder_1_out_6), .out_7(decoder_1_out_6));
  and and_1 (D5, A5, WE);
  and and_2 (D4, A4, WE);
  and and_3 (D3, A3, WE);
  and and_4 (D2, A2, WE);
  and and_5 (D1, A1, WE);
  and and_6 (D0, A0, WE);
  _5bit_reg _5bit_reg_1 (.Din_4_0(Wrd_4_0), .Sel(D5), .CLK(CLK), .Dout_4_0(R5));
  _5bit_reg _5bit_reg_2 (.Din_4_0(Wrd_4_0), .Sel(D4), .CLK(CLK), .Dout_4_0(R4));
  _5bit_reg _5bit_reg_3 (.Din_4_0(Wrd_4_0), .Sel(D3), .CLK(CLK), .Dout_4_0(R3));
  _5bit_reg _5bit_reg_4 (.Din_4_0(Wrd_4_0), .Sel(D2), .CLK(CLK), .Dout_4_0(R2));
  _5bit_reg _5bit_reg_5 (.Din_4_0(Wrd_4_0), .Sel(D1), .CLK(CLK), .Dout_4_0(R1));
  _5bit_reg _5bit_reg_6 (.Din_4_0(Wrd_4_0), .Sel(D0), .CLK(CLK), .Dout_4_0(R0));
  Multiplexer #(.Selector_Bits(3), .Bits(5)) multiplexer_1 (
    .sel(RA_2_0), .in_0(R0), .in_1(R1), .in_2(R2), .in_3(R3), .in_4(R4), .in_5(R5), .in_6({5{1'b0}}),
    .in_7({5{1'b0}}), .out(A_4_0));
  Multiplexer #(.Selector_Bits(3), .Bits(5)) multiplexer_2 (
    .sel(RB_2_0), .in_0(R0), .in_1(R1), .in_2(R2), .in_3(R3), .in_4(R4), .in_5(R5), .in_6({5{1'b0}}),
    .in_7({5{1'b0}}), .out(B_4_0));
  // also tied to GND on the sheet: decoder_1_out_6
endmodule
