// Digital circuit 8x15 SRAM.dig as structural Verilog
module _8x15_SRAM (
  input  [14:0] Wrd_14_0,
  input  [2:0] WA_2_0,
  input  [2:0] RA1_2_0,
  input  [2:0] RA2_2_0,
  input  CLK,
  input  WE,
  output [14:0] RD1_14_0,
  output [14:0] RD2_14_0
);

  wire RS1_0, RS1_1, RS1_2, RS1_3, RS1_4, RS1_5, RS1_6, RS1_7, RS2_0, RS2_1, RS2_2, RS2_3, RS2_4, RS2_5,
       RS2_6, RS2_7, W0, W1, W2, W3, W4, W5, W6, W7, WS_0, WS_1, WS_2, WS_3, WS_4, WS_5, WS_6, WS_7;
  wire [14:0] RD1_0, RD1_1, RD1_2, RD1_3, RD1_4, RD1_5, RD1_6, RD1_7, RD2_0, RD2_1, RD2_2, RD2_3, RD2_4,
       RD2_5, RD2_6, RD2_7;

  Decoder #(.Selector_Bits(3)) decoder_1 (
    .sel(RA1_2_0), .out_0(RS1_0), .out_1(RS1_1), .out_2(RS1_2), .out_3(RS1_3), .out_4(RS1_4), .out_5(RS1_5),
    .out_6(RS1_6), .out_7(RS1_7));
  Decoder #(.Selector_Bits(3)) decoder_2 (
    .sel(RA2_2_0), .out_0(RS2_0), .out_1(RS2_1), .out_2(RS2_2), .out_3(RS2_3), .out_4(RS2_4), .out_5(RS2_5),
    .out_6(RS2_6), .out_7(RS2_7));
  Decoder #(.Selector_Bits(3)) decoder_3 (
    .sel(WA_2_0), .out_0(W0), .out_1(W1), .out_2(W2), .out_3(W3), .out_4(W4), .out_5(W5), .out_6(W6),
    .out_7(W7));
  and and_1 (WS_0, W0, WE);
  and and_2 (WS_1, W1, WE);
  and and_3 (WS_2, W2, WE);
  and and_4 (WS_3, W3, WE);
  _1x15_SRAM _1x15_sram_1 (
    .RS1(RS1_0), .RS2(RS2_0), .WS(WS_0), .WD_14_0(Wrd_14_0), .CLK(CLK), .RD1_14_0(RD1_0), .RD2_14_0(RD2_0));
  _1x15_SRAM _1x15_sram_2 (
    .RS1(RS1_1), .RS2(RS2_1), .WS(WS_1), .WD_14_0(Wrd_14_0), .CLK(CLK), .RD1_14_0(RD1_1), .RD2_14_0(RD2_1));
  _1x15_SRAM _1x15_sram_3 (
    .RS1(RS1_2), .RS2(RS2_2), .WS(WS_2), .WD_14_0(Wrd_14_0), .CLK(CLK), .RD1_14_0(RD1_2), .RD2_14_0(RD2_2));
  _1x15_SRAM _1x15_sram_4 (
    .RS1(RS1_3), .RS2(RS2_3), .WS(WS_3), .WD_14_0(Wrd_14_0), .CLK(CLK), .RD1_14_0(RD1_3), .RD2_14_0(RD2_3));
  and and_5 (WS_4, W4, WE);
  and and_6 (WS_5, W5, WE);
  and and_7 (WS_6, W6, WE);
  and and_8 (WS_7, W7, WE);
  _1x15_SRAM _1x15_sram_5 (
    .RS1(RS1_4), .RS2(RS2_4), .WS(WS_4), .WD_14_0(Wrd_14_0), .CLK(CLK), .RD1_14_0(RD1_4), .RD2_14_0(RD2_4));
  _1x15_SRAM _1x15_sram_6 (
    .RS1(RS1_5), .RS2(RS2_5), .WS(WS_5), .WD_14_0(Wrd_14_0), .CLK(CLK), .RD1_14_0(RD1_5), .RD2_14_0(RD2_5));
  _1x15_SRAM _1x15_sram_7 (
    .RS1(RS1_6), .RS2(RS2_6), .WS(WS_6), .WD_14_0(Wrd_14_0), .CLK(CLK), .RD1_14_0(RD1_6), .RD2_14_0(RD2_6));
  _1x15_SRAM _1x15_sram_8 (
    .RS1(RS1_7), .RS2(RS2_7), .WS(WS_7), .WD_14_0(Wrd_14_0), .CLK(CLK), .RD1_14_0(RD1_7), .RD2_14_0(RD2_7));
  assign RD1_14_0 = RD1_0 | RD1_1 | RD1_2 | RD1_3 | RD1_4 | RD1_5 | RD1_6 | RD1_7;  // Or or_1, 15 bits wide
  assign RD2_14_0 = RD2_0 | RD2_1 | RD2_2 | RD2_3 | RD2_4 | RD2_5 | RD2_6 | RD2_7;  // Or or_2, 15 bits wide

  // Other names for the same wires on the sheet: Wrd[14:0] = Wrd_14_0
endmodule
