// Digital circuit 4bit CU.dig as structural Verilog
module _4bit_CU (
  input  [3:0] Opcode_3_0,
  input  ZF,
  input  SF,
  output [1:0] Op_1_0,
  output Imm_sel,
  output Jmp_sel,
  output REG_EN
);

  wire and_1_out, and_2_out, and_4_out, and_5_out, and_6_out, and_7_out, or_1_out, or_2_out, or_3_out,
       or_4_out;

  or or_1 (or_1_out, ZF, ~SF);  // Or
  and and_1 (and_1_out, Opcode_3_0[0], ~Opcode_3_0[1]);  // And
  and and_2 (and_2_out, ~Opcode_3_0[2], ~Opcode_3_0[3]);  // And
  and and_3 (Imm_sel, Opcode_3_0[2], ~Opcode_3_0[3]);  // And
  and and_4 (and_4_out, ~Opcode_3_0[2], Opcode_3_0[3]);  // And
  and and_5 (and_5_out, ~Opcode_3_0[0], ~Opcode_3_0[1]);  // And
  and and_6 (and_6_out, Opcode_3_0[0], ~Opcode_3_0[1], or_1_out);  // And
  or or_2 (or_2_out, and_2_out, Imm_sel);
  or or_3 (or_3_out, and_5_out, and_6_out);
  and and_7 (and_7_out, and_1_out, or_2_out);
  or or_4 (or_4_out, and_7_out, and_4_out);
  and and_8 (Jmp_sel, and_4_out, or_3_out);
  not not_1 (REG_EN, or_4_out);

  assign Op_1_0 = Opcode_3_0[1:0];

  // Other names for the same wires on the sheet: jump_type[1:0] = Opcode_3_0[1:0]

  // Notes on the sheet:
  //   CMP
  //   REG
  //   Imm
  //   jmp_op
  //   JMP
  //   JGE
endmodule
