// Digital circuit 4bit program counter.dig as structural Verilog
module _4bit_program_counter (
  input  CLK,
  input  [3:0] Din_3_0,
  output [3:0] Dout_3_0
);

  // _1bit_reg _1bit_reg_1: pin names not known; wires that end beside it: Din_3_0[0], 1'b1, CLK, Dout_3_0[0]
  // _1bit_reg _1bit_reg_2: pin names not known; wires that end beside it: Din_3_0[1], 1'b1, CLK, Dout_3_0[1]
  // _1bit_reg _1bit_reg_3: pin names not known; wires that end beside it: Din_3_0[2], 1'b1, CLK, Dout_3_0[2]
  // _1bit_reg _1bit_reg_4: pin names not known; wires that end beside it: Din_3_0[3], 1'b1, CLK, Dout_3_0[3]

  // Other names for the same wires on the sheet: D_0 = Din_3_0[0]; D_1 = Din_3_0[1]; D_2 = Din_3_0[2];
  //   D_3 = Din_3_0[3]; O_0 = Dout_3_0[0]; O_1 = Dout_3_0[1]; O_2 = Dout_3_0[2]; O_3 = Dout_3_0[3]
endmodule
