// Digital circuit 5bit CPU new.dig as structural Verilog
module _5bit_CPU_new (
  input  [17:0] Wrd_17_0,
  input  CLK,
  input  WE,
  input  PC_EN,
  input  [3:0] Wr_3_0,
  output [17:0] RD2_17_0,
  output [4:0] result,
  output [1:0] reg1,
  output [1:0] reg2,
  output [4:0] reg1_value,
  output [1:0] op,
  output [4:0] value_part
);

  wire CPU_CLK, Imm_sel, JMP_SEL, REG_EN, SF, ZF;
  wire [2:0] value;
  wire [3:0] _4bit_pc_adder_1_o_3_0, _4bit_program_counter_1_dout_3_0, multiplexer_1_out, Opcode;
  wire [4:0] _5bitreg_set_1_b_4_0;
  wire [6:0] XX;

  Multiplexer #(.Bits(4)) multiplexer_1 (
    .sel(JMP_SEL), .in_0(_4bit_pc_adder_1_o_3_0), .in_1({reg1, reg2}), .out(multiplexer_1_out));
  _4bit_program_counter _4bit_program_counter_1 (
    .Din_3_0(multiplexer_1_out), .CLK(CPU_CLK), .Dout_3_0(_4bit_program_counter_1_dout_3_0));
  _4bit_PC_adder _4bit_pc_adder_1 (.I_3_0(_4bit_program_counter_1_dout_3_0), .O_3_0(_4bit_pc_adder_1_o_3_0));
  and and_1 (CPU_CLK, PC_EN, CLK);
  _9x18_SRAM _9x18_sram_1 (
    .RA1_3_0(_4bit_program_counter_1_dout_3_0), .RA2_3_0(4'b0000), .WA_3_0(Wr_3_0), .Wrd_17_0(Wrd_17_0),
    .WE(WE), .CLK(CLK), .RD1_17_0({Opcode, reg1, reg2, value, XX}), .RD2_17_0(RD2_17_0));
  _5bitREG_set _5bitreg_set_1 (
    .Wrd_4_0(result), .Wr_1_0(reg1), .WE(REG_EN), .CLK(CPU_CLK), .RA_1_0(reg1), .RB_1_0(reg2),
    .A_4_0(reg1_value), .B_4_0(_5bitreg_set_1_b_4_0));
  _4bit_CU _4bit_cu_1 (
    .Opcode_3_0(Opcode), .ZF(ZF), .SF(SF), .Op_1_0(op), .REG_EN(REG_EN), .Imm_sel(Imm_sel), .Jmp_sel(JMP_SEL));
  _5bitALU _5bitalu_1 (.A_4_0(reg1_value), .B_4_0(value_part), .OP_1_0(op), .ZF(ZF), .SF(SF), .O_4_0(result));
  Multiplexer #(.Bits(5)) multiplexer_2 (
    .sel(Imm_sel), .in_0(_5bitreg_set_1_b_4_0), .in_1({reg2, value}), .out(value_part));

  // Other names for the same wires on the sheet: JMP_ADDRESS[3:0] = {reg1, reg2}; value[4:3] = reg2;
  //   A[4:0] = reg1_value; B[4:0] = value_part; RD2[17:0] = RD2_17_0; Wr[3:0] = Wr_3_0; Wrd[17:0] = Wrd_17_0
endmodule
