// Digital circuit 5bit XOR.dig as structural Verilog
module _5bit_XOR (
  input  [4:0] A_4_0,
  input  [4:0] B_4_0,
  output [4:0] O_4_0
);

  xor xor_1 (O_4_0[0], A_4_0[0], B_4_0[0]);
  xor xor_2 (O_4_0[1], A_4_0[1], B_4_0[1]);
  xor xor_3 (O_4_0[2], A_4_0[2], B_4_0[2]);
  xor xor_4 (O_4_0[3], A_4_0[3], B_4_0[3]);
  xor xor_5 (O_4_0[4], A_4_0[4], B_4_0[4]);

  // Other names for the same wires on the sheet: A_0 = A_4_0[0]; A_1 = A_4_0[1]; A_2 = A_4_0[2]; A_3 = A_4_0[3];
  //   A_4 = A_4_0[4]; B_0 = B_4_0[0]; B_1 = B_4_0[1]; B_2 = B_4_0[2]; B_3 = B_4_0[3]; B_4 = B_4_0[4]; O_0 = O_4_0[0];
  //   O_1 = O_4_0[1]; O_2 = O_4_0[2]; O_3 = O_4_0[3]; O_4 = O_4_0[4]
endmodule
