// Digital circuit 5bitADD_SUB.dig as structural Verilog
module _5bitADD_SUB (
  input  [4:0] A_4_0,
  input  [4:0] B_4_0,
  input  Sel,
  output [4:0] O_4_0,
  output CF
);

  wire fa_2_cout, fa_3_cout, fa_4_cout, fa_5_cout, xor_1_out, xor_2_out, xor_3_out, xor_4_out, xor_5_out;

  xor xor_1 (xor_1_out, B_4_0[4], Sel);
  FA fa_1 (.X(A_4_0[4]), .Y(xor_1_out), .Cin(fa_2_cout), .S(O_4_0[4]), .Cout(CF));
  xor xor_2 (xor_2_out, B_4_0[3], Sel);
  FA fa_2 (.X(A_4_0[3]), .Y(xor_2_out), .Cin(fa_3_cout), .S(O_4_0[3]), .Cout(fa_2_cout));
  xor xor_3 (xor_3_out, B_4_0[2], Sel);
  FA fa_3 (.X(A_4_0[2]), .Y(xor_3_out), .Cin(fa_4_cout), .S(O_4_0[2]), .Cout(fa_3_cout));
  xor xor_4 (xor_4_out, B_4_0[1], Sel);
  FA fa_4 (.X(A_4_0[1]), .Y(xor_4_out), .Cin(fa_5_cout), .S(O_4_0[1]), .Cout(fa_4_cout));
  xor xor_5 (xor_5_out, B_4_0[0], Sel);
  FA fa_5 (.X(A_4_0[0]), .Y(xor_5_out), .Cin(Sel), .S(O_4_0[0]), .Cout(fa_5_cout));

  // Other names for the same wires on the sheet: A_0 = A_4_0[0]; A_1 = A_4_0[1]; A_2 = A_4_0[2]; A_3 = A_4_0[3];
  //   A_4 = A_4_0[4]; B_0 = B_4_0[0]; B_1 = B_4_0[1]; B_2 = B_4_0[2]; B_3 = B_4_0[3]; B_4 = B_4_0[4]; M = Sel;
  //   O_0 = O_4_0[0]; O_1 = O_4_0[1]; O_2 = O_4_0[2]; O_3 = O_4_0[3]; O_4 = O_4_0[4]
endmodule
