// Digital circuit 5bitALU.dig as structural Verilog
module _5bitALU (
  input  [4:0] A_4_0,
  input  [4:0] B_4_0,
  input  [1:0] OP_1_0,
  output ZF,
  output SF,
  output [4:0] O_4_0
);

  wire or_1_out;
  wire [4:0] _5bit_shr_1_o_4_0, _5bit_xor_1_o_4_0, _5bitadd_sub_1_o_4_0;

  _5bit_XOR _5bit_xor_1 (.A_4_0(A_4_0), .B_4_0(B_4_0), .O_4_0(_5bit_xor_1_o_4_0));
  _5bitADD_SUB _5bitadd_sub_1 (
    .A_4_0(A_4_0), .B_4_0(B_4_0), .Sel(OP_1_0[1]), .O_4_0(_5bitadd_sub_1_o_4_0));  // open: CF
  _5bit_SHR _5bit_shr_1 (.A_4_0(A_4_0), .B_4_0(B_4_0), .O_4_0(_5bit_shr_1_o_4_0));
  Multiplexer #(.Selector_Bits(2), .Bits(5)) multiplexer_1 (
    .sel(OP_1_0), .in_0(_5bit_xor_1_o_4_0), .in_1(_5bitadd_sub_1_o_4_0), .in_2(_5bitadd_sub_1_o_4_0),
    .in_3(_5bit_shr_1_o_4_0), .out(O_4_0));
  or or_1 (or_1_out, O_4_0[0], O_4_0[1], O_4_0[2], O_4_0[3], O_4_0[4]);
  not not_1 (ZF, or_1_out);

  assign SF = O_4_0[4];

  // Other names for the same wires on the sheet: A[4:0] = A_4_0; B[4:0] = B_4_0; OP_0 = OP_1_0[0]; OP_1 = OP_1_0[1];
  //   R[4:0] = O_4_0
endmodule
