// Digital circuit 5bit_SHR.dig as structural Verilog
module _5bit_SHR (
  input  [4:0] A_4_0,
  input  [4:0] B_4_0,
  output [4:0] O_4_0
);

  Multiplexer #(.Selector_Bits(3)) multiplexer_1 (
    .sel(B_4_0[2:0]), .in_0(A_4_0[4]), .in_1(1'b0), .in_2(1'b0), .in_3(1'b0), .in_4(1'b0), .in_5(1'b0),
    .in_6(1'b0), .in_7(1'b0), .out(O_4_0[4]));
  Multiplexer #(.Selector_Bits(3)) multiplexer_2 (
    .sel(B_4_0[2:0]), .in_0(A_4_0[3]), .in_1(A_4_0[4]), .in_2(1'b0), .in_3(1'b0), .in_4(1'b0), .in_5(1'b0),
    .in_6(1'b0), .in_7(1'b0), .out(O_4_0[3]));
  Multiplexer #(.Selector_Bits(3)) multiplexer_3 (
    .sel(B_4_0[2:0]), .in_0(A_4_0[2]), .in_1(A_4_0[3]), .in_2(A_4_0[4]), .in_3(1'b0), .in_4(1'b0),
    .in_5(1'b0), .in_6(1'b0), .in_7(1'b0), .out(O_4_0[2]));
  Multiplexer #(.Selector_Bits(3)) multiplexer_4 (
    .sel(B_4_0[2:0]), .in_0(A_4_0[1]), .in_1(A_4_0[2]), .in_2(A_4_0[3]), .in_3(A_4_0[4]), .in_4(1'b0),
    .in_5(1'b0), .in_6(1'b0), .in_7(1'b0), .out(O_4_0[1]));
  Multiplexer #(.Selector_Bits(3)) multiplexer_5 (
    .sel(B_4_0[2:0]), .in_0(A_4_0[0]), .in_1(A_4_0[1]), .in_2(A_4_0[2]), .in_3(A_4_0[3]), .in_4(A_4_0[4]),
    .in_5(1'b0), .in_6(1'b0), .in_7(1'b0), .out(O_4_0[0]));

  // Other names for the same wires on the sheet: A_0 = A_4_0[0]; A_1 = A_4_0[1]; A_2 = A_4_0[2]; A_3 = A_4_0[3];
  //   A_4 = A_4_0[4]; B_2_0[2:0] = B_4_0[2:0]; O_0 = O_4_0[0]; O_1 = O_4_0[1]; O_2 = O_4_0[2]; O_3 = O_4_0[3];
  //   O_4 = O_4_0[4]
endmodule
