// Digital circuit 5bit_reg.dig as structural Verilog
module _5bit_reg (
  input  Sel,
  input  CLK,
  input  [4:0] Din_4_0,
  output [4:0] Dout_4_0
);

  // _1bit_reg _1bit_reg_1: pin names not known; wires that end beside it: Din_4_0[0], Sel, CLK, Dout_4_0[0]
  // _1bit_reg _1bit_reg_2: pin names not known; wires that end beside it: Din_4_0[1], Sel, CLK, Dout_4_0[1]
  // _1bit_reg _1bit_reg_3: pin names not known; wires that end beside it: Din_4_0[2], Sel, CLK, Dout_4_0[2]
  // _1bit_reg _1bit_reg_4: pin names not known; wires that end beside it: Din_4_0[3], Sel, CLK, Dout_4_0[3]
  // _1bit_reg _1bit_reg_5: pin names not known; wires that end beside it: Din_4_0[4], Sel, CLK, Dout_4_0[4]

  // Other names for the same wires on the sheet: D_0 = Din_4_0[0]; D_1 = Din_4_0[1]; D_2 = Din_4_0[2];
  //   D_3 = Din_4_0[3]; D_4 = Din_4_0[4]; O_0 = Dout_4_0[0]; O_1 = Dout_4_0[1]; O_2 = Dout_4_0[2]; O_3 = Dout_4_0[3];
  //   O_4 = Dout_4_0[4]
endmodule
