// Digital circuit 9x18 SRAM.dig as structural Verilog
module _9x18_SRAM (
  input  [17:0] Wrd_17_0,
  input  [3:0] WA_3_0,
  input  [3:0] RA1_3_0,
  input  [3:0] RA2_3_0,
  input  CLK,
  input  WE,
  output [17:0] RD1_17_0,
  output [17:0] RD2_17_0
);

  wire RS1_0, RS1_1, RS1_2, RS1_3, RS1_4, RS1_5, RS1_6, RS1_7, RS1_8, RS2_0, RS2_1, RS2_2, RS2_3, RS2_4,
       RS2_5, RS2_6, RS2_7, RS2_8, W0, W1, W2, W3, W4, W5, W6, W7, W8, WS_0, WS_1, WS_2, WS_3, WS_4, WS_5,
       WS_6, WS_7, WS_8;
  wire [17:0] RD1_0, RD1_1, RD1_2, RD1_3, RD1_4, RD1_5, RD1_6, RD1_7, RD1_8, RD2_0, RD2_1, RD2_2, RD2_3,
       RD2_4, RD2_5, RD2_6, RD2_7, RD2_8;

  Decoder #(.Selector_Bits(4)) decoder_1 (
    .sel(RA2_3_0), .out_0(RS2_0), .out_1(RS2_1), .out_2(RS2_2), .out_3(RS2_3), .out_4(RS2_4), .out_5(RS2_5),
    .out_6(RS2_6), .out_7(RS2_7), .out_8(RS2_8));  // open: out_9, out_10, out_11, out_12, out_13, out_14, out_15
  Decoder #(.Selector_Bits(4)) decoder_2 (
    .sel(WA_3_0), .out_0(W0), .out_1(W1), .out_2(W2), .out_3(W3), .out_4(W4), .out_5(W5), .out_6(W6),
    .out_7(W7), .out_8(W8));  // open: out_9, out_10, out_11, out_12, out_13, out_14, out_15
  Decoder #(.Selector_Bits(4)) decoder_3 (
    .sel(RA1_3_0), .out_0(RS1_0), .out_1(RS1_1), .out_2(RS1_2), .out_3(RS1_3), .out_4(RS1_4), .out_5(RS1_5),
    .out_6(RS1_6), .out_7(RS1_7), .out_8(RS1_8));  // open: out_9, out_10, out_11, out_12, out_13, out_14, out_15
  and and_1 (WS_0, W0, WE);
  and and_2 (WS_1, W1, WE);
  and and_3 (WS_2, W2, WE);
  _1x18_SRAM _1x18_sram_1 (
    .RS1(RS1_0), .RS2(RS2_0), .WS(WS_0), .WD_17_0(Wrd_17_0), .CLK(CLK), .RD1_17_0(RD1_0), .RD2_17_0(RD2_0));
  _1x18_SRAM _1x18_sram_2 (
    .RS1(RS1_1), .RS2(RS2_1), .WS(WS_1), .WD_17_0(Wrd_17_0), .CLK(CLK), .RD1_17_0(RD1_1), .RD2_17_0(RD2_1));
  _1x18_SRAM _1x18_sram_3 (
    .RS1(RS1_2), .RS2(RS2_2), .WS(WS_2), .WD_17_0(Wrd_17_0), .CLK(CLK), .RD1_17_0(RD1_2), .RD2_17_0(RD2_2));
  and and_4 (WS_3, W3, WE);
  and and_5 (WS_4, W4, WE);
  and and_6 (WS_5, W5, WE);
  _1x18_SRAM _1x18_sram_4 (
    .RS1(RS1_3), .RS2(RS2_3), .WS(WS_3), .WD_17_0(Wrd_17_0), .CLK(CLK), .RD1_17_0(RD1_3), .RD2_17_0(RD2_3));
  _1x18_SRAM _1x18_sram_5 (
    .RS1(RS1_4), .RS2(RS2_4), .WS(WS_4), .WD_17_0(Wrd_17_0), .CLK(CLK), .RD1_17_0(RD1_4), .RD2_17_0(RD2_4));
  _1x18_SRAM _1x18_sram_6 (
    .RS1(RS1_5), .RS2(RS2_5), .WS(WS_5), .WD_17_0(Wrd_17_0), .CLK(CLK), .RD1_17_0(RD1_5), .RD2_17_0(RD2_5));
  and and_7 (WS_6, W6, WE);
  and and_8 (WS_7, W7, WE);
  and and_9 (WS_8, W8, WE);
  _1x18_SRAM _1x18_sram_7 (
    .RS1(RS1_6), .RS2(RS2_6), .WS(WS_6), .WD_17_0(Wrd_17_0), .CLK(CLK), .RD1_17_0(RD1_6), .RD2_17_0(RD2_6));
  _1x18_SRAM _1x18_sram_8 (
    .RS1(RS1_7), .RS2(RS2_7), .WS(WS_7), .WD_17_0(Wrd_17_0), .CLK(CLK), .RD1_17_0(RD1_7), .RD2_17_0(RD2_7));
  _1x18_SRAM _1x18_sram_9 (
    .RS1(RS1_8), .RS2(RS2_8), .WS(WS_8), .WD_17_0(Wrd_17_0), .CLK(CLK), .RD1_17_0(RD1_8), .RD2_17_0(RD2_8));
  assign RD1_17_0 = RD1_0 | RD1_1 | RD1_2 | RD1_3 | RD1_4 | RD1_5 | RD1_6 | RD1_7 | RD1_8;  // Or or_1, 18 bits wide
  assign RD2_17_0 = RD2_0 | RD2_1 | RD2_2 | RD2_3 | RD2_4 | RD2_5 | RD2_6 | RD2_7 | RD2_8;  // Or or_2, 18 bits wide

  // Other names for the same wires on the sheet: Wrd[17:0] = Wrd_17_0
endmodule
