// Digital circuit ALU 6bit.dig as structural Verilog
module ALU_6bit (
  input  [5:0] A_5_0,
  input  [5:0] B_5_0,
  input  [1:0] OP_1_0,
  output [5:0] O_5_0,
  output ZF
);

  wire or_1_out;
  wire [5:0] add_6bit_1_p4, not_6bit_1_p2, ror_6bit_1_p3;

  // NOT_6bit not_6bit_1: pin names not known; wires that end beside it: A_5_0, not_6bit_1_p2
  // ADD_6bit add_6bit_1: pin names not known; wires that end beside it: A_5_0, B_5_0, OP_1_0[1], add_6bit_1_p4
  // ROR_6bit ror_6bit_1: pin names not known; wires that end beside it: A_5_0, B_5_0, ror_6bit_1_p3
  Multiplexer #(.Selector_Bits(2), .Bits(6)) multiplexer_1 (
    .sel(OP_1_0), .in_0(not_6bit_1_p2), .in_1(add_6bit_1_p4), .in_2(ror_6bit_1_p3), .in_3({6{1'b0}}),
    .out(O_5_0));
  or or_1 (or_1_out, O_5_0[0], O_5_0[1], O_5_0[2], O_5_0[3], O_5_0[4], O_5_0[5]);
  not not_1 (ZF, or_1_out);

  // Other names for the same wires on the sheet: A[5:0] = A_5_0; B[5:0] = B_5_0; OP_0 = OP_1_0[0]; OP_1 = OP_1_0[1];
  //   R[5:0] = O_5_0
endmodule
